// Logisim project ArrayMulti.circ as structural Verilog: 1 circuit, main circuit main
module main (
  input  in_1,
  input  in_2,
  input  in_3,
  input  in_4,
  input  in_5,
  input  in_6,
  output out_7,
  output out_8,
  output out_9,
  output out_10,
  output out_11,
  output out_12
);

  wire adder_1_cout, adder_2_cout, adder_2_out, adder_3_cout, adder_3_out, adder_5_cout, adder_6_cout,
       and_2_out, and_3_out, and_4_out, and_5_out, and_6_out, and_7_out, and_8_out, and_9_out;

  and and_1 (out_7, in_3, in_6);
  and and_2 (and_2_out, in_2, in_6);
  and and_3 (and_3_out, in_3, in_5);
  and and_4 (and_4_out, in_1, in_6);
  and and_5 (and_5_out, in_2, in_5);
  and and_6 (and_6_out, in_3, in_4);
  and and_7 (and_7_out, in_1, in_5);
  and and_8 (and_8_out, in_2, in_4);
  and and_9 (and_9_out, in_1, in_4);
  Adder #(.width(1)) adder_1 (.a(and_2_out), .b(and_3_out), .out(out_8), .cout(adder_1_cout));  // open: cin
  Adder #(.width(1)) adder_2 (.a(and_4_out), .b(and_5_out), .out(adder_2_out), .cout(adder_2_cout));  // open: cin
  Adder #(.width(1)) adder_3 (.a(and_7_out), .b(and_8_out), .out(adder_3_out), .cin(adder_2_cout), .cout(adder_3_cout));
  Adder #(.width(1)) adder_4 (.a(and_9_out), .b(adder_6_cout), .out(out_11), .cin(adder_3_cout), .cout(out_12));
  Adder #(.width(1)) adder_5 (.a(adder_2_out), .b(and_6_out), .out(out_9), .cin(adder_1_cout), .cout(adder_5_cout));
  Adder #(.width(1)) adder_6 (.a(adder_3_out), .b(adder_5_cout), .out(out_10), .cout(adder_6_cout));  // open: cin
endmodule
